# Fritzing sketch wiring (saved by Fritzing 0.9.3b)

parts:
  S3 = SWITCH-MOMENTARY-2 [package=reed_switch_pth]
  Windrichtungsanzeige = SWITCH-MOMENTARY-2 [package=reed_switch_pth]
  S5 = SWITCH-MOMENTARY-2 [package=reed_switch_pth]
  S6 = SWITCH-MOMENTARY-2 [package=reed_switch_pth]
  S7 = SWITCH-MOMENTARY-2 [package=reed_switch_pth]
  S8 = SWITCH-MOMENTARY-2 [package=reed_switch_pth]
  S9 = SWITCH-MOMENTARY-2 [package=reed_switch_pth]
  S10 = SWITCH-MOMENTARY-2 [package=reed_switch_pth]
  Regenmengenmesser = SWITCH-MOMENTARY-2 [package=reed_switch_pth]
  Bauteil1 = Arduino Pro Mini (3.3V)
  BME280 = BME280 Breakout
  Config-Taster = Momentary Switch [package=ksa_sealed_tac_switch]
  Anemometer = SWITCH-MOMENTARY-2 [package=reed_switch_pth]  # not connected
  R4 = Resistor [tolerance=±5% resistance=3.9k package=THT]
  R5 = Resistor [tolerance=±5% resistance=8.2k package=THT]
  R6 = Resistor [tolerance=±5% resistance=120k package=THT]
  R7 = Resistor [tolerance=±5% resistance=5.6k package=THT]
  R8 = Resistor [tolerance=±5% resistance=2.2k package=THT]
  R9 = Resistor [tolerance=±5% resistance=64.9k package=THT]
  R10 = Resistor [tolerance=±5% resistance=24k package=THT]
  R11 = Resistor [tolerance=±5% resistance=16k package=THT]
  C4 = Ceramic Capacitor [capacitance="100 nF" package="1206 [SMD, multilayer]"]
  C5 = Ceramic Capacitor [capacitance="100 nF" package="1206 [SMD, multilayer]"]
  Antenne_~8_3cm = CC1101 [part_number=CC1101]
  Bauteil2 = VEML6070 [part_number=VEML6070]  # not connected
  R12 = Resistor [tolerance=±5% resistance=100 package=THT]
  R13 = Resistor [tolerance=±5% resistance=100 package=THT]
  JP1 = Header 11 [package=1x11_smd_no_holes]
  Regensensor_(stall_biz) = YL-83 Rain Sensor - Detection Board
  C6 = Ceramic Capacitor [capacitance=1nF package="1206 [SMD, multilayer]"]
  R14 = Resistor [tolerance=±5% resistance=100k package=THT]
  Q1 = NPN-Transistor [part_number="MPSA13 o.ä." package="TO92 [THT]"]
  R15 = Resistor [tolerance=±5% resistance=10k package=THT]
  MAX44009 = MAX44009

nets:
  N1: S3.1, R6.Pin_0
  N2: Windrichtungsanzeige.1, R5.Pin_1
  GND: S5.1, Regenmengenmesser.1, Bauteil1.GND, BME280.GND, Config-Taster.4, C4.1, Antenne_~8_3cm.2, JP1.1, JP1.2, JP1.3, JP1.5, JP1.10, Regensensor_(stall_biz).POS, Q1.E, MAX44009.GND
  N3: S5.2, R7.Pin_1
  N4: S6.1, R4.Pin_0
  N5: S7.1, R10.Pin_0
  N6: S8.1, R8.Pin_1
  N7: S9.2, R9.Pin_0
  N8: S10.2, R11.Pin_1
  N9: Regenmengenmesser.2, R12.Pin_1
  N10: Bauteil1.A4, BME280.SDI/SDA, MAX44009.SDA
  N11: Bauteil1.A5, BME280.SCK/SCL, MAX44009.SCL
  VCC: Bauteil1.VCC, BME280.3.3V, Antenne_~8_3cm.1, JP1.11, MAX44009.VCC
  N12: Bauteil1.A3, C6.1, R14.Pin_1
  N13: Bauteil1.A2, R8.Pin_0
  N14: Bauteil1.SCK, Antenne_~8_3cm.4, JP1.9
  N15: Bauteil1.MISO, Antenne_~8_3cm.5, JP1.7
  N16: Bauteil1.MOSI, Antenne_~8_3cm.3, JP1.8
  N17: Bauteil1.D10, Antenne_~8_3cm.8
  N18: Bauteil1.D9, R15.Pin_1
  N19: Bauteil1.D8, Config-Taster.3
  N20: Bauteil1.D7, JP1.6
  N21: Bauteil1.D6, C4.0, R12.Pin_0
  N22: Bauteil1.D5, C5.0, R13.Pin_0
  N23: Bauteil1.D4, R14.Pin_0
  N24: Bauteil1.D3, JP1.4
  N25: Bauteil1.D2, Antenne_~8_3cm.7
  N26: R4.Pin_1, R11.Pin_0
  N27: Regensensor_(stall_biz).NEG, C6.0
  N28: Q1.B, R15.Pin_0

notes:
  VCC
  (z.B. 5V Netzteil) an RAW / GND
  falls ein anderes Regendetektor-Modell (mit Schaltausgang!) angeschlossen werden soll, ist dessen Ausgang an Pin 9 anzuschließen und der Sketch entsprechend anzupassen:
  // #define USE_RAINDETECTOR_STALLBIZ

custom parts:
  VEML6070: This little sensor is a great way to add UV light sensing to any microcontroller project. The VEML6070 from Vishay has a true UV A light sensor and an I2C-controlled ADC that will take readings and integrate them for you over ~60ms to 500ms.
  YL-83 Rain Sensor - Detection Board: The YL-83 is a rain sensor that has more resistance when dry and less resistance when wet. The module runs at 5V.
  MAX44009: Light Sensor
